// Logisim project 2s_complement_decoder.circ as structural Verilog: 1 circuit, main circuit main
module main (
  input  Neg,
  input  Cin,
  input  \input ,
  input  Neg_2,
  input  input_2,
  input  Cin_2,
  output Out,
  output Cout,
  output Out_2,
  output Cout_2
);

  wire and_1_out, and_2_out, not_1_out, not_2_out, xor_1_out;

  not not_1 (not_1_out, Cin);
  not not_2 (not_2_out, \input );
  xor xor_1 (xor_1_out, Neg_2, input_2);
  and and_1 (and_1_out, xor_1_out, Cin_2);
  and and_2 (and_2_out, Neg, not_1_out);
  and and_3 (Cout, Cin, not_2_out);
  xor xor_2 (Out_2, xor_1_out, Cin_2);
  and and_4 (Cout_2, Neg_2, and_1_out);
  xor xor_3 (Out, \input , and_2_out);
endmodule
