// Logisim project 4-bit_shift_add_3.circ as structural Verilog: 1 circuit, main circuit main
module main (
  input  A,
  input  B,
  input  C,
  input  D,
  input  B_2,
  input  C_2,
  input  in_7,
  input  A_2,
  input  B_3,
  input  C_3,
  input  in_11,
  input  A_3,
  input  B_4,
  input  C_4,
  input  in_15,
  input  in_16,
  input  A_4,
  input  B_5,
  input  C_5,
  input  in_20,
  output out_21,
  output out_22,
  output out_23,
  output out_24,
  output out_25,
  output out_26,
  output out_27,
  output out_28,
  output out_29,
  output out_30,
  output out_31,
  output out_32,
  output out_33,
  output out_34,
  output out_35,
  output out_36
);

  wire _1_2_out, _1_3_out, _1_4_out, _1_5_out, _1_6_out, _1_7_out, _1_8_out, _1_9_out, _1_out, _2_2_out,
       _2_3_out, _2_4_out, _2_5_out, _2_6_out, _2_7_out, _2_8_out, _2_9_out, _2_out, _3_2_out, _3_3_out,
       _3_4_out, _3_5_out, _3_6_out, _3_7_out, _3_8_out, _3_9_out, _3_out, _4_2_out, _4_3_out, _4_4_out,
       _4_5_out, _4_6_out, _4_7_out, _4_8_out, _4_9_out, _4_out, _5_2_out, _5_3_out, _5_4_out, _5_5_out,
       _5_6_out, _5_7_out, _5_8_out, _5_9_out, _5_out, _6_2_out, _6_3_out, _6_4_out, _6_5_out, _6_6_out,
       _6_7_out, _6_8_out, _6_9_out, _6_out, _7_2_out, _7_3_out, _7_4_out, _7_5_out, _7_6_out, _7_7_out,
       _7_8_out, _7_9_out, _7_out, _8_2_out, _8_3_out, _8_4_out, _8_5_out, _8_6_out, _8_7_out, _8_8_out,
       _8_9_out, _8_out, _9_2_out, _9_3_out, _9_4_out, _9_5_out, _9_6_out, _9_7_out, _9_8_out, _9_9_out,
       _9_out, _10_2_out, _10_3_out, _10_4_out, _10_5_out, _10_6_out, _10_7_out, _11_2_out, _11_3_out,
       _11_4_out, _11_5_out, _11_6_out, _11_7_out, _11_8_out, _11_9_out, _11_out, _12_2_out, _12_3_out,
       _12_4_out, _12_5_out, _12_6_out, _12_7_out, _12_8_out, _12_9_out, _12_out, _13_2_out, _13_3_out,
       _13_4_out, _13_5_out, _13_6_out, _13_7_out, _13_8_out, _13_9_out, _13_out, _14_2_out, _14_3_out,
       _14_4_out, _14_5_out, _14_6_out, _14_7_out, _15_2_out, _15_3_out, _15_4_out, _15_5_out, _15_6_out,
       _15_7_out, _15_8_out, _15_9_out, _15_out, _16_2_out, _16_3_out, _16_4_out, _16_5_out, _16_6_out,
       _16_7_out, _17_2_out, _17_3_out, _17_4_out, _17_5_out, _17_6_out, _17_7_out, _17_8_out, _17_9_out,
       _17_out, _18_2_out, _18_3_out, _18_4_out, _18_5_out, _18_7_out, not_1_out, not_2_out, not_3_out,
       not_4_out, not_5_out, not_6_out, not_7_out, not_8_out, not_9_out, not_10_out, not_11_out, not_12_out,
       not_13_out, not_14_out, not_15_out, not_16_out, not_17_out, not_18_out, not_19_out, not_20_out,
       not_21_out, not_22_out, not_23_out, not_24_out, not_25_out, not_26_out, not_27_out;

  not _1 (_1_out, A);
  not _2 (_2_out, B);
  and _7 (_7_out, B, C);
  and _13 (_13_out, A, D);
  not _4 (_4_out, D);
  not _3 (_3_out, C);
  not _1_2 (_1_2_out, A_2);
  not _2_2 (_2_2_out, B_3);
  not _3_2 (_3_2_out, C_3);
  not _4_2 (_4_2_out, in_11);
  or _8 (_8_out, A, _7_out);
  and _15 (_15_out, A, _4_out);
  and _5 (_5_out, B, _4_out, _3_out);
  and _7_2 (_7_2_out, _1_2_out, in_11, _2_2_out);
  and _6 (_6_out, B_3, C_3);
  and _5_2 (_5_2_out, B_3, _3_2_out, _4_2_out);
  not _1_3 (_1_3_out, A_4);
  not _2_3 (_2_3_out, B_5);
  not _3_3 (_3_3_out, C_5);
  not _4_3 (_4_3_out, in_20);
  and _6_2 (_6_2_out, _1_out, D, _2_out);
  or _11 (_11_out, _2_out, D);
  not not_1 (not_1_out, _8_out);
  or _8_2 (_8_2_out, A_2, _6_out);
  and _5_3 (_5_3_out, B_5, _3_3_out, _4_3_out);
  and _12 (_12_out, _11_out, C);
  or _14 (out_22, _13_out, _5_out);
  or _9 (_9_out, not_1_out, D);
  not not_2 (not_2_out, _8_2_out);
  or _9_2 (_9_2_out, not_2_out, in_11);
  and _7_3 (_7_3_out, _1_3_out, in_20, _2_3_out);
  and _6_3 (_6_3_out, B_5, C_5);
  not not_3 (not_3_out, _9_out);
  not not_4 (not_4_out, _9_2_out);
  or _8_3 (_8_3_out, A_4, _6_3_out);
  not not_5 (not_5_out, _8_3_out);
  not not_6 (not_6_out, _17_out);
  or _17 (_17_out, _2_out, out_22);
  or _16 (out_23, _12_out, _15_out);
  or _10 (out_24, _6_2_out, not_3_out);
  or _10_2 (_10_2_out, _7_2_out, not_4_out);
  not not_7 (not_7_out, _9_3_out);
  or _9_3 (_9_3_out, not_5_out, in_20);
  or _18 (out_21, A, not_6_out);
  or _12_2 (_12_2_out, _2_2_out, in_11);
  and _11_2 (_11_2_out, A_2, _4_2_out);
  or _10_3 (_10_3_out, _7_3_out, not_7_out);
  and _13_2 (_13_2_out, _12_2_out, C_3);
  and _11_3 (_11_3_out, A_4, _4_3_out);
  or _14_2 (_14_2_out, _13_2_out, _11_2_out);
  or _12_3 (_12_3_out, _2_3_out, in_20);
  and _15_2 (_15_2_out, A_2, in_11);
  or _16_2 (_16_2_out, _15_2_out, _5_2_out);
  and _13_3 (_13_3_out, _12_3_out, C_5);
  or _17_2 (_17_2_out, _2_2_out, _16_2_out);
  and _15_3 (_15_3_out, A_4, in_20);
  or _14_3 (_14_3_out, _13_3_out, _11_3_out);
  not not_8 (not_8_out, _17_2_out);
  or _16_3 (_16_3_out, _15_3_out, _5_3_out);
  or _18_2 (_18_2_out, A_2, not_8_out);
  not not_9 (not_9_out, _17_3_out);
  or _17_3 (_17_3_out, _2_3_out, _16_3_out);
  or _18_3 (_18_3_out, A_4, not_9_out);
  not _1_4 (_1_4_out, _16_2_out);
  not _2_4 (_2_4_out, _14_2_out);
  not _3_4 (_3_4_out, _10_2_out);
  not _4_4 (_4_4_out, A_3);
  and _7_4 (_7_4_out, _1_4_out, A_3, _2_4_out);
  and _6_4 (_6_4_out, _14_2_out, _10_2_out);
  and _5_4 (_5_4_out, _14_2_out, _3_4_out, _4_4_out);
  not not_10 (not_10_out, _8_4_out);
  or _8_4 (_8_4_out, _16_2_out, _6_4_out);
  or _9_4 (_9_4_out, not_10_out, A_3);
  or _10_4 (_10_4_out, _7_4_out, not_11_out);
  not not_11 (not_11_out, _9_4_out);
  and _11_4 (_11_4_out, _16_2_out, _4_4_out);
  or _12_4 (_12_4_out, _2_4_out, A_3);
  and _13_4 (_13_4_out, _12_4_out, _10_2_out);
  or _14_4 (_14_4_out, _13_4_out, _11_4_out);
  and _15_4 (_15_4_out, _16_2_out, A_3);
  or _16_4 (_16_4_out, _15_4_out, _5_4_out);
  or _17_4 (_17_4_out, _2_4_out, _16_4_out);
  not not_12 (not_12_out, _17_4_out);
  or _18_4 (_18_4_out, _16_2_out, not_12_out);
  not _1_5 (_1_5_out, _16_4_out);
  not _2_5 (_2_5_out, _14_4_out);
  not _3_5 (_3_5_out, _10_4_out);
  and _5_5 (_5_5_out, _14_4_out, _3_5_out, _4_5_out);
  not _4_5 (_4_5_out, B_4);
  and _7_5 (_7_5_out, _1_5_out, B_4, _2_5_out);
  and _6_5 (_6_5_out, _14_4_out, _10_4_out);
  not not_13 (not_13_out, _8_5_out);
  or _8_5 (_8_5_out, _16_4_out, _6_5_out);
  or _9_5 (_9_5_out, not_13_out, B_4);
  not not_14 (not_14_out, _9_5_out);
  or _10_5 (_10_5_out, _7_5_out, not_14_out);
  and _11_5 (_11_5_out, _16_4_out, _4_5_out);
  or _12_5 (_12_5_out, _2_5_out, B_4);
  and _13_5 (_13_5_out, _12_5_out, _10_4_out);
  and _15_5 (_15_5_out, _16_4_out, B_4);
  or _14_5 (_14_5_out, _13_5_out, _11_5_out);
  or _16_5 (_16_5_out, _15_5_out, _5_5_out);
  not not_15 (not_15_out, _17_5_out);
  or _17_5 (_17_5_out, _2_5_out, _16_5_out);
  or _18_5 (_18_5_out, _16_4_out, not_15_out);
  not _1_6 (_1_6_out, in_7);
  not _2_6 (_2_6_out, _18_2_out);
  not _3_6 (_3_6_out, _18_4_out);
  not _4_6 (_4_6_out, _18_5_out);
  not _1_7 (_1_7_out, _16_5_out);
  not _2_7 (_2_7_out, _14_5_out);
  not _3_7 (_3_7_out, _10_5_out);
  not _4_7 (_4_7_out, C_4);
  and _5_6 (_5_6_out, _18_2_out, _3_6_out, _4_6_out);
  and _7_6 (_7_6_out, _1_7_out, C_4, _2_7_out);
  and _6_6 (_6_6_out, _14_5_out, _10_5_out);
  and _5_7 (_5_7_out, _14_5_out, _3_7_out, _4_7_out);
  and _7_7 (_7_7_out, _1_6_out, _18_5_out, _2_6_out);
  and _6_7 (_6_7_out, _18_2_out, _18_4_out);
  or _8_6 (_8_6_out, _16_5_out, _6_6_out);
  not not_16 (not_16_out, _8_7_out);
  or _8_7 (_8_7_out, in_7, _6_7_out);
  not not_17 (not_17_out, _8_6_out);
  or _9_6 (_9_6_out, not_16_out, _18_5_out);
  not not_18 (not_18_out, _9_6_out);
  or _9_7 (_9_7_out, not_17_out, C_4);
  not not_19 (not_19_out, _9_7_out);
  or _10_6 (_10_6_out, _7_7_out, not_18_out);
  or _10_7 (_10_7_out, _7_6_out, not_19_out);
  and _11_6 (_11_6_out, in_7, _4_6_out);
  and _11_7 (_11_7_out, _16_5_out, _4_7_out);
  or _12_6 (_12_6_out, _2_6_out, _18_5_out);
  or _12_7 (_12_7_out, _2_7_out, C_4);
  and _13_6 (_13_6_out, _12_7_out, _10_5_out);
  and _13_7 (_13_7_out, _12_6_out, _18_4_out);
  or _14_6 (_14_6_out, _13_6_out, _11_7_out);
  and _15_6 (_15_6_out, in_7, _18_5_out);
  or _14_7 (_14_7_out, _13_7_out, _11_6_out);
  and _15_7 (_15_7_out, _16_5_out, C_4);
  or _16_6 (_16_6_out, _15_6_out, _5_6_out);
  or _16_7 (_16_7_out, _15_7_out, _5_7_out);
  not not_20 (not_20_out, _17_6_out);
  or _17_6 (_17_6_out, _2_6_out, _16_6_out);
  not not_21 (not_21_out, _17_7_out);
  or _17_7 (_17_7_out, _2_7_out, _16_7_out);
  or _18_6 (out_27, in_7, not_20_out);
  or _18_7 (_18_7_out, _16_5_out, not_21_out);
  not _1_8 (_1_8_out, _16_6_out);
  not _2_8 (_2_8_out, _14_7_out);
  not _3_8 (_3_8_out, _10_6_out);
  not _4_8 (_4_8_out, _18_7_out);
  not _1_9 (_1_9_out, _16_7_out);
  not _2_9 (_2_9_out, _14_6_out);
  not _3_9 (_3_9_out, _10_7_out);
  not _4_9 (_4_9_out, in_15);
  and _7_8 (_7_8_out, _1_8_out, _18_7_out, _2_8_out);
  and _6_8 (_6_8_out, _14_7_out, _10_6_out);
  and _5_8 (_5_8_out, _14_7_out, _3_8_out, _4_8_out);
  and _7_9 (_7_9_out, _1_9_out, in_15, _2_9_out);
  and _6_9 (_6_9_out, _14_6_out, _10_7_out);
  and _5_9 (_5_9_out, _14_6_out, _3_9_out, _4_9_out);
  or _8_8 (_8_8_out, _16_6_out, _6_8_out);
  or _8_9 (_8_9_out, _16_7_out, _6_9_out);
  not not_22 (not_22_out, _8_9_out);
  not not_23 (not_23_out, _8_8_out);
  or _9_8 (_9_8_out, not_23_out, _18_7_out);
  or _9_9 (_9_9_out, not_22_out, in_15);
  not not_24 (not_24_out, _9_8_out);
  or _10_8 (out_35, _7_9_out, not_25_out);
  not not_25 (not_25_out, _9_9_out);
  or _10_9 (out_31, _7_8_out, not_24_out);
  and _11_8 (_11_8_out, _16_7_out, _4_9_out);
  or _12_8 (_12_8_out, _2_8_out, _18_7_out);
  and _11_9 (_11_9_out, _16_6_out, _4_8_out);
  or _12_9 (_12_9_out, _2_9_out, in_15);
  and _13_8 (_13_8_out, _12_8_out, _10_6_out);
  and _13_9 (_13_9_out, _12_9_out, _10_7_out);
  or _14_8 (out_30, _13_8_out, _11_9_out);
  and _15_8 (_15_8_out, _16_7_out, in_15);
  or _14_9 (out_34, _13_9_out, _11_8_out);
  and _15_9 (_15_9_out, _16_6_out, _18_7_out);
  or _16_8 (out_29, _15_9_out, _5_8_out);
  or _16_9 (out_33, _15_8_out, _5_9_out);
  or _17_8 (_17_8_out, _2_8_out, out_29);
  or _17_9 (_17_9_out, _2_9_out, out_33);
  not not_26 (not_26_out, _17_8_out);
  or _18_8 (out_32, _16_7_out, not_27_out);
  not not_27 (not_27_out, _17_9_out);
  or _18_9 (out_28, _16_6_out, not_26_out);

  assign out_25 = B_2;
  assign out_26 = C_2;
  assign out_36 = in_16;

  // Notes on the sheet:
  //   D
endmodule
