// Logisim project d-latch.circ as structural Verilog: 7 circuits, main circuit main
module main (
  input  M2_2,
  input  M2_1,
  input  m1_2,
  input  m1_1,
  input  d2,
  input  d1,
  input  a2,
  input  a1,
  input  s,
  output m2_2_out,
  output m1_2_out,
  output m1_1_out,
  output m2_1_out,
  output o2,
  output o1
);

  wire and_1_out, and_2_out, and_3_out, and_4_out, and_5_out, and_6_out, and_7_out, nor_1_out, not_1_out;

  and and_1 (and_1_out, and_3_out, m2_2_out);
  or or_1 (o2, and_1_out, and_5_out);
  and and_2 (and_2_out, and_3_out, m2_1_out, m2_1_out, m2_1_out);
  or or_2 (o1, and_2_out, and_6_out);
  d_latch d_latch_1 (.Q(M2_1), .D(d1), .S(and_4_out), .out_4(m2_1_out));
  d_latch d_latch_2 (.Q(M2_2), .D(d2), .S(and_4_out), .out_4(m2_2_out));
  not not_1 (not_1_out, a2);
  and and_3 (and_3_out, not_1_out, a1);
  and and_4 (and_4_out, s, and_3_out);
  and and_5 (and_5_out, nor_1_out, m1_2_out);
  and and_6 (and_6_out, nor_1_out, m1_1_out);
  d_latch d_latch_3 (.Q(m1_1), .D(d1), .S(and_7_out), .out_4(m1_1_out));
  d_latch d_latch_4 (.Q(m1_2), .D(d2), .S(and_7_out), .out_4(m1_2_out));
  nor nor_1 (nor_1_out, a2, a1);
  and and_7 (and_7_out, s, nor_1_out);

  // Notes on the sheet:
  //   Mem2
  //   Mem 1
  //   data
  //   address
  //   set
endmodule

module d_latch (
  input  Q,
  input  D,
  input  S,
  output out_4
);

  wire and_1_out, and_2_out, not_1_out;

  and and_1 (and_1_out, Q, not_1_out);
  or or_1 (out_4, and_1_out, and_2_out);
  not not_1 (not_1_out, S);
  and and_2 (and_2_out, D, S);
endmodule

module b (
  input  Q,
  input  D,
  input  S,
  output out_4
);

  wire and_1_out, and_2_out, not_1_out;

  and and_1 (and_1_out, Q, not_1_out);
  not not_1 (not_1_out, S);
  and and_2 (and_2_out, D, S);
  or or_1 (out_4, and_1_out, and_2_out);
endmodule

module c (
);

  b b_1 ();  // open: Q, D, S, out_4
endmodule

module selector (
  input  in_1,
  input  in_2,
  input  in_3,
  input  in_4,
  output out_5
);

  wire xnor_1_out, xnor_2_out;

  xnor xnor_1 (xnor_1_out, in_1, in_3);
  xnor xnor_2 (xnor_2_out, in_2, in_4);
  and and_1 (out_5, xnor_1_out, xnor_2_out);
endmodule

module _2_bit_selector_lite (
  input  a,
  input  b,
  input  c,
  input  d,
  output x
);

  wire xnor_1_out, xnor_2_out;

  xnor xnor_1 (xnor_1_out, a, c);
  xnor xnor_2 (xnor_2_out, b, d);
  and and_1 (x, xnor_1_out, xnor_2_out);
endmodule

module d (
  input  in_1,
  output out_2
);


  assign out_2 = in_1;
endmodule
